# Fritzing sketch pcb (saved by Fritzing 0.9.3b)
circuit board: 7.7081cm x 5.37977cm
breadboards: 1

parts:
  U1 = atmega328 [package=dip]
  C3 = Ceramic Capacitor [capacitance="100 nF" package="0603 [SMD, multilayer]"]
  J1 = Basic Servo
  Part2 = Bluetooth HC-05 Macho
  C2 = Ceramic Capacitor [capacitance=20µF package="0805 [SMD, multilayer]"]
  XTAL1 = Crystal [frequency="16 Mhz" package=THT]
  C1 = Ceramic Capacitor [capacitance=20µF package="0805 [SMD, multilayer]"]
  Part3 = FTDI Basic Programmer

nets (from the schematic view):
  N1: U1.RESET, C3.0
  N2: U1.D0_(RX), Part2.RXD, Part3.TXO
  N3: U1.D1_(TX), Part2.TXD, Part3.RXI
  N4: U1.VCC, Part3.POWER
  N5: U1.GND#7, C2.0, C1.0
  N6: U1.XLAT1, XTAL1.pin_0, C1.1
  N7: U1.XLAT2, C2.1, XTAL1.pin_1
  N8: U1.D13, J1.pulse
  VCC: U1.AVCC, J1.vcc, Part2.VCC
  GND: U1.GND#21, J1.gnd, Part2.GND, Part3.GND
  N9: C3.1, Part3.DTR
